# Fritzing sketch 電控 (saved by Fritzing 0.9.3b)
breadboards: 1

parts:
  元件1 = Arduino Uno (Rev3)
  元件2 = Arduino Uno (Rev3)
  S2 = H-Bridge with L298N
  M1 = DC Motor
  BAT1 = Battery Holders [package=battery-aa-kit]
  M2 = DC Motor
  S4 = H-Bridge with L298N
  M3 = DC Motor
  M7 = DC Motor
  M8 = DC Motor
  R1 = Resistor [tolerance=±5% resistance=4.7k package=THT]
  R2 = Resistor [tolerance=±5% resistance=4.7k package=THT]
  BS1 = BASIC Stamp 2e
  S6 = H-Bridge with L298N
  J2 = Basic Servo
  J1 = Basic Servo

nets:
  N1: 元件1.A2, 元件1.RESET
  N2: 元件1.A4/SDA, 元件2.A4/SDA, R1.Pin_1
  N3: 元件1.A5/SCL, 元件2.A5/SCL, R2.Pin_0
  N4: 元件1.D8, S6.IN2
  N5: 元件1.D9_PWM, S6.IN3
  N6: 元件1.D10_PWM/SS, S6.IN4
  N7: 元件1.D11_PWM/MOSI, S6.ENB
  GND: 元件1.GND, 元件2.GND, S2.GND, BAT1.-, S4.GND, BS1.P15, S6.GND, J2.gnd, J1.gnd
  N8: 元件1.D3_PWM, J2.pulse
  N9: 元件1.D5_PWM, J1.pulse
  N10: 元件1.D6_PWM, S6.ENA
  N11: 元件1.D7, S6.IN1
  5V: 元件1.5V, 元件2.5V, R1.Pin_0, R2.Pin_1, S6.5V, J2.vcc, J1.vcc
  N12: 元件2.A1, S4.IN1
  N13: 元件2.A2, 元件2.RESET
  N14: 元件2.D8, S2.IN1
  N15: 元件2.D9_PWM, S2.ENA
  N16: 元件2.D10_PWM/SS, BS1.VIN
  N17: 元件2.D11_PWM/MOSI, BS1.VSS
  N18: 元件2.D12/MISO, BS1.RES
  N19: 元件2.D13/SCK, BS1.VDD
  N20: 元件2.D2, S4.IN2
  N21: 元件2.D3_PWM, S4.ENA, S4.ENA-5V
  N22: 元件2.D4, S2.IN4
  N23: 元件2.D5_PWM, S2.IN3
  N24: 元件2.D6_PWM, S2.ENB
  N25: 元件2.D7, S2.IN2
  N26: 元件2.3V3, BS1.P8
  12V: S2.12V, S4.12V
  N27: S2.M1-01, M1.pin_2
  N28: S2.M1-02, M1.pin_1
  N29: S2.M2-01, M2.pin_2
  N30: S2.M2-02, M2.pin_1
  N31: BAT1.+, S6.12V
  N32: S4.M2-01, M3.pin_2
  N33: S4.M2-02, M3.pin_1
  N34: M7.pin_1, S6.M1-02
  N35: M7.pin_2, S6.M1-01
  N36: M8.pin_1, S6.M2-02
  N37: M8.pin_2, S6.M2-01

notes:
  PS2
  依照上各所給的教材PDF接法
  底盤輪子馬達_左
  底盤輪子馬達_右
  Master
  中心
  升降馬達
  夾爪馬達
  手臂伸縮馬達
  置物盒
  開關馬達
  置物盒伸縮馬達
  電池僅為示意圖
  非真實樣貌
  Slave
  被操控
  18650
  電池三顆串聯
  11.1V

custom parts:
  H-Bridge with L298N: h-bridge
